# Fritzing sketch connection (saved by Fritzing 0.9.2b)
breadboards: 1

parts:
  U1 = NodeMCU V1.0
  Bauteil1 = Arduino Nano (Rev3.0)
  JP2 = Header 8 [package=1x08_smd_alt]
  JP3 = Header 8 [package=1x08_smd_alt]

nets:
  N1: U1.D0, JP3.2
  N2: U1.D1, Bauteil1.D8, JP2.2, JP3.1
  N3: U1.D4, JP3.8
  GND: U1.GND, Bauteil1.GND, JP2.1, JP2.5, JP2.7
  N4: U1.D5, JP2.8
  N5: U1.D6, JP3.7
  N6: U1.D7, JP3.6
  N7: U1.D8, JP2.6
  N8: U1.RX, JP3.5
  N9: U1.RSV#40, Bauteil1.VIN
  N10: Bauteil1.A4, JP2.3
  N11: Bauteil1.A3, JP3.3
  N12: Bauteil1.A2, JP2.4
  N13: Bauteil1.A1, JP3.4

custom parts:
  NodeMCU V1.0: ESP9266 based NodeMCU
